// Digital circuit halfAdder.dig as structural Verilog
module halfAdder (
  input  i_A,
  input  i_B,
  output o_Cout,
  output o_S
);

  Decoder #(.Selector_Bits(2)) decoder_1 (.sel({i_B, i_A}), .out_3(o_Cout));  // open: out_0, out_1, out_2
  LookUpTable lookuptable_1 (.in0(i_A), .in1(i_B), .out(o_S));

  // Notes on the sheet:
  //   contents of lookuptable_1 (hex, n*v repeats v):
  //   0,1,1
endmodule

/* Test case Tests:
i_A i_B o_S o_Cout
0 0 0 0 
0 1 1 0
1 0 1 0
1 1 0 1
*/
